// Logisim project Final draft design.circ as structural Verilog
module PC (
  input  [19:0] Common_Bus,
  input  in_2,
  input  in_3,
  input  in_4,
  input  in_5,
  output [19:0] OUT
);

  wire or_1_out;
  wire [13:0] adder_1_out, multiplexer_1_out;

  Multiplexer #(.width(14), .enable("false")) multiplexer_1 (
    .in0(Common_Bus[13:0]), .in1(adder_1_out), .out(multiplexer_1_out), .sel(in_4));
  Adder #(.width(14)) adder_1 (.a(14'h1), .b(OUT[13:0]), .out(adder_1_out));  // open: cin, cout
  or or_1 (or_1_out, in_4, in_3);
  Register #(.width(14)) register_1 (.D(multiplexer_1_out), .en(or_1_out), .Q(OUT[13:0]), .clk(in_5), .clr(in_2));

  assign OUT[19:14] = {6{1'b0}};
endmodule

// PC Control
module PC_control (
  input  [19:0] IR,
  input  [2:0] SC,
  input  [19:0] AC,
  input  [19:0] DR,
  input  R,
  input  FGI,
  input  FGO,
  input  E,
  output Load,
  output Increment,
  output Clear
);

  wire and_3_out, and_4_out, and_5_out, and_6_out, and_7_out, and_8_out, and_9_out, and_10_out, and_11_out,
       and_12_out, and_13_out, decoder_1_out0, decoder_1_out1, decoder_1_out2, decoder_1_out3,
       decoder_1_out4, decoder_1_out5, decoder_1_out6, decoder_1_out7, decoder_2_out0, decoder_2_out1,
       decoder_2_out2, decoder_2_out3, decoder_2_out4, decoder_2_out5, decoder_2_out6, decoder_2_out7,
       decoder_2_out8, decoder_2_out9, decoder_2_out10, decoder_2_out11, decoder_2_out12, decoder_2_out13,
       decoder_2_out14, decoder_2_out15, or_1_out, or_2_out, p, r_t;

  Decoder #(.select(3)) decoder_1 (
    .out0(decoder_1_out0), .out1(decoder_1_out1), .out2(decoder_1_out2), .out3(decoder_1_out3),
    .out4(decoder_1_out4), .out5(decoder_1_out5), .out6(decoder_1_out6), .out7(decoder_1_out7), .sel(SC));  // open: en
  Decoder #(.select(4)) decoder_2 (
    .out0(decoder_2_out0), .out1(decoder_2_out1), .out2(decoder_2_out2), .out3(decoder_2_out3),
    .out4(decoder_2_out4), .out5(decoder_2_out5), .out6(decoder_2_out6), .out7(decoder_2_out7),
    .out8(decoder_2_out8), .out9(decoder_2_out9), .out10(decoder_2_out10), .out11(decoder_2_out11),
    .out12(decoder_2_out12), .out13(decoder_2_out13), .out14(decoder_2_out14), .out15(decoder_2_out15),
    .sel(IR[17:14]));  // open: en
  and and_1 (p, decoder_1_out3, IR[19], IR[18], decoder_2_out15);
  and and_2 (r_t, decoder_2_out0, decoder_1_out3, IR[19], IR[18]);
  or or_1 (or_1_out, AC[19], AC[18], AC[17], AC[16], AC[15], AC[14], AC[13], AC[12], AC[11], AC[10], AC[8], AC[7], AC[6], AC[5], AC[4], AC[3], AC[2], AC[1], AC[0], AC[9]);
  and and_3 (and_3_out, decoder_1_out5, decoder_2_out6);
  and and_4 (and_4_out, decoder_2_out7, decoder_1_out6);
  and and_5 (and_5_out, ~R, decoder_1_out1);  // AND_Gate
  and and_6 (and_6_out, R, decoder_1_out3);
  and and_7 (and_7_out, decoder_2_out8, ~or_2_out, decoder_1_out6);  // AND_Gate
  and and_8 (and_8_out, IR[6], r_t, ~AC[19]);  // AND_Gate
  and and_9 (and_9_out, IR[5], r_t, AC[19]);
  and and_10 (and_10_out, IR[4], r_t, or_1_out);
  and and_11 (and_11_out, IR[3], r_t, E);
  and and_12 (and_12_out, IR[11], p, FGI);
  and and_13 (and_13_out, IR[10], p, FGO);
  or or_2 (or_2_out, DR[19], DR[18], DR[17], DR[16], DR[15], DR[14], DR[13], DR[12], DR[11], DR[10], DR[8], DR[7], DR[6], DR[5], DR[4], DR[3], DR[2], DR[1], DR[0], DR[9]);
  or or_3 (Load, and_3_out, and_4_out);
  or or_4 (Increment, and_5_out, and_6_out, and_7_out, and_8_out, and_9_out, and_10_out, and_11_out, and_12_out, and_13_out);
  and and_14 (Clear, R, decoder_1_out2);

  // Notes on the sheet:
  //   3x8 decoder
  //   4x8 decoder
  //   D6T5
  //   D7T6
endmodule

module AC (
  input  [19:0] ALU,
  input  Incr,
  input  Clear,
  input  Load,
  input  in_5,
  output [19:0] Output
);

  wire or_1_out;
  wire [19:0] adder_1_out, multiplexer_1_out;

  Adder #(.width(20)) adder_1 (.a(20'h1), .b(Output), .out(adder_1_out));  // open: cin, cout
  Multiplexer #(.width(20), .enable("false")) multiplexer_1 (
    .in0(ALU), .in1(adder_1_out), .out(multiplexer_1_out), .sel(Incr));
  or or_1 (or_1_out, Incr, Load);
  Register #(.width(20)) register_1 (.D(multiplexer_1_out), .en(or_1_out), .Q(Output), .clk(in_5), .clr(Clear));

  // Notes on the sheet:
  //   AC ko load check garna parne xa CBS bata aauxa ki nai?
endmodule

module AC_control (
  input  [19:0] IR,
  input  [2:0] SC,
  output Load,
  output Clear,
  output Increment
);

  wire and_1_out, and_2_out, and_3_out, and_4_out, and_5_out, and_6_out, and_7_out, and_8_out, and_9_out,
       decoder_1_out0, decoder_1_out1, decoder_1_out2, decoder_1_out3, decoder_1_out4, decoder_1_out5,
       decoder_1_out6, decoder_1_out7, decoder_2_out0, decoder_2_out1, decoder_2_out2, decoder_2_out3,
       decoder_2_out4, decoder_2_out5, decoder_2_out6, decoder_2_out7, decoder_2_out8, decoder_2_out9,
       decoder_2_out10, decoder_2_out11, decoder_2_out12, decoder_2_out13, decoder_2_out14, decoder_2_out15,
       p, r;

  Decoder #(.select(3)) decoder_1 (
    .out0(decoder_1_out0), .out1(decoder_1_out1), .out2(decoder_1_out2), .out3(decoder_1_out3),
    .out4(decoder_1_out4), .out5(decoder_1_out5), .out6(decoder_1_out6), .out7(decoder_1_out7), .sel(SC));  // open: en
  Decoder #(.select(4)) decoder_2 (
    .out0(decoder_2_out0), .out1(decoder_2_out1), .out2(decoder_2_out2), .out3(decoder_2_out3),
    .out4(decoder_2_out4), .out5(decoder_2_out5), .out6(decoder_2_out6), .out7(decoder_2_out7),
    .out8(decoder_2_out8), .out9(decoder_2_out9), .out10(decoder_2_out10), .out11(decoder_2_out11),
    .out12(decoder_2_out12), .out13(decoder_2_out13), .out14(decoder_2_out14), .out15(decoder_2_out15),
    .sel(IR[17:14]));  // open: en
  and and_1 (and_1_out, decoder_2_out0, decoder_1_out5);
  and and_2 (and_2_out, decoder_2_out1, decoder_1_out5);
  and and_3 (and_3_out, decoder_2_out2, decoder_1_out5);
  and and_4 (and_4_out, decoder_2_out3, decoder_1_out5);
  and and_5 (and_5_out, decoder_2_out4, decoder_1_out5);
  and and_6 (and_6_out, decoder_2_out9, decoder_1_out6);
  and and_7 (and_7_out, IR[9], r);
  and and_8 (and_8_out, IR[8], r);
  and and_9 (and_9_out, IR[11], p);
  and and_10 (p, decoder_1_out3, IR[19], IR[18], decoder_2_out15);
  and and_11 (r, decoder_2_out0, decoder_1_out3, IR[19], IR[18]);
  or or_1 (Load, and_1_out, and_2_out, and_3_out, and_4_out, and_5_out, and_6_out, and_7_out, and_8_out, and_9_out);
  and and_12 (Clear, IR[13], r);
  and and_13 (Increment, IR[7], p);

  // Notes on the sheet:
  //   3x8 decoder
  //   4x8 decoder
endmodule

module AR (
  input  [19:0] Common_Bus,
  input  Clear,
  input  Load,
  input  INcrement,
  input  Clk,
  output [19:0] OUT
);

  wire or_1_out;
  wire [13:0] adder_1_out, multiplexer_1_out;

  Multiplexer #(.width(14)) multiplexer_1 (
    .in0(Common_Bus[13:0]), .in1(adder_1_out), .out(multiplexer_1_out), .sel(INcrement));  // open: en
  or or_1 (or_1_out, INcrement, Load);
  Register #(.width(14)) register_1 (.D(multiplexer_1_out), .en(or_1_out), .Q(OUT[13:0]), .clk(Clk), .clr(Clear));
  Adder #(.width(14)) adder_1 (.a(14'h1), .b(OUT[13:0]), .out(adder_1_out));  // open: cin, cout

  assign OUT[19:14] = {6{1'b0}};
endmodule

module AR_control (
  input  [19:0] IR,
  input  R,
  input  [2:0] SC,
  output Load,
  output Clear,
  output Increment
);

  wire and_1_out, and_2_out, and_3_out, decoder_1_out0, decoder_1_out1, decoder_1_out2, decoder_1_out3,
       decoder_1_out4, decoder_1_out5, decoder_1_out6, decoder_1_out7, decoder_2_out0, decoder_2_out1,
       decoder_2_out2, decoder_2_out3, decoder_2_out4, decoder_2_out5, decoder_2_out6, decoder_2_out7,
       decoder_2_out8, decoder_2_out9, decoder_2_out10, decoder_2_out11, decoder_2_out12, decoder_2_out13,
       decoder_2_out14, decoder_2_out15;

  Decoder #(.select(3)) decoder_1 (
    .out0(decoder_1_out0), .out1(decoder_1_out1), .out2(decoder_1_out2), .out3(decoder_1_out3),
    .out4(decoder_1_out4), .out5(decoder_1_out5), .out6(decoder_1_out6), .out7(decoder_1_out7), .sel(SC));  // open: en
  Decoder #(.select(4)) decoder_2 (
    .out0(decoder_2_out0), .out1(decoder_2_out1), .out2(decoder_2_out2), .out3(decoder_2_out3),
    .out4(decoder_2_out4), .out5(decoder_2_out5), .out6(decoder_2_out6), .out7(decoder_2_out7),
    .out8(decoder_2_out8), .out9(decoder_2_out9), .out10(decoder_2_out10), .out11(decoder_2_out11),
    .out12(decoder_2_out12), .out13(decoder_2_out13), .out14(decoder_2_out14), .out15(decoder_2_out15),
    .sel(IR[17:14]));  // open: en
  and and_1 (and_1_out, ~R, decoder_1_out0);  // AND_Gate
  and and_2 (and_2_out, ~decoder_2_out0, ~decoder_2_out15, decoder_1_out3, ~IR[18], ~IR[19]);  // AND_Gate
  and and_3 (and_3_out, ~R, decoder_1_out2);  // AND_Gate
  and and_4 (Clear, R, decoder_1_out1);
  and and_5 (Increment, decoder_2_out7, decoder_1_out5);
  or or_1 (Load, and_1_out, and_2_out, and_3_out);
endmodule

module DR (
  input  [19:0] CBS_Mockup,
  input  Incr,
  input  Load,
  input  in_4,
  output [19:0] out_5
);

  wire button_1_out, or_1_out;
  wire [19:0] adder_1_out, multiplexer_1_out;

  or or_1 (or_1_out, Load, Incr);
  Multiplexer #(.width(20), .enable("false")) multiplexer_1 (
    .in0(CBS_Mockup), .in1(adder_1_out), .out(multiplexer_1_out), .sel(Incr));
  Adder #(.width(20)) adder_1 (.a(20'h1), .b(out_5), .out(adder_1_out));  // open: cin, cout
  Button button_1 (.out(button_1_out));
  Register #(.width(20)) DR (.D(multiplexer_1_out), .en(or_1_out), .Q(out_5), .clk(in_4), .clr(button_1_out));
endmodule

// DR Control
module DR_control (
  input  [19:0] IR,
  input  [2:0] SC,
  output Load,
  output Increment
);

  wire and_1_out, and_2_out, and_3_out, and_4_out, decoder_1_out0, decoder_1_out1, decoder_1_out2,
       decoder_1_out3, decoder_1_out4, decoder_1_out5, decoder_1_out6, decoder_1_out7, decoder_2_out0,
       decoder_2_out1, decoder_2_out2, decoder_2_out3, decoder_2_out4, decoder_2_out5, decoder_2_out6,
       decoder_2_out7, decoder_2_out8, decoder_2_out9, decoder_2_out10, decoder_2_out11, decoder_2_out12,
       decoder_2_out13, decoder_2_out14, decoder_2_out15;

  Decoder #(.select(3)) decoder_1 (
    .out0(decoder_1_out0), .out1(decoder_1_out1), .out2(decoder_1_out2), .out3(decoder_1_out3),
    .out4(decoder_1_out4), .out5(decoder_1_out5), .out6(decoder_1_out6), .out7(decoder_1_out7), .sel(SC));  // open: en
  Decoder #(.select(4)) decoder_2 (
    .out0(decoder_2_out0), .out1(decoder_2_out1), .out2(decoder_2_out2), .out3(decoder_2_out3),
    .out4(decoder_2_out4), .out5(decoder_2_out5), .out6(decoder_2_out6), .out7(decoder_2_out7),
    .out8(decoder_2_out8), .out9(decoder_2_out9), .out10(decoder_2_out10), .out11(decoder_2_out11),
    .out12(decoder_2_out12), .out13(decoder_2_out13), .out14(decoder_2_out14), .out15(decoder_2_out15),
    .sel(IR[17:14]));  // open: en
  and and_1 (and_1_out, ~decoder_2_out0, ~decoder_2_out15, decoder_1_out3, ~IR[19], ~IR[18]);  // AND_Gate
  and and_2 (and_2_out, ~decoder_2_out0, ~decoder_2_out15, decoder_1_out4, ~IR[19], IR[18]);  // AND_Gate
  and and_3 (and_3_out, ~decoder_2_out0, ~decoder_2_out15, decoder_1_out3, IR[19], ~IR[18]);  // AND_Gate
  and and_4 (and_4_out, decoder_2_out9, decoder_1_out6);
  and and_5 (Increment, decoder_2_out8, decoder_1_out5);
  or or_1 (Load, and_1_out, and_2_out, and_3_out, and_4_out);
endmodule

module IR (
  input  [19:0] CBS_Mockup,
  input  Load,
  input  in_3,
  output [19:0] out_4
);

  wire button_1_out;

  Button button_1 (.out(button_1_out));
  Register #(.width(20)) IR (.D(CBS_Mockup), .en(Load), .Q(out_4), .clk(in_3), .clr(button_1_out));
endmodule

module IR_control (
  input  [2:0] SC,
  input  R,
  output Load
);

  wire decoder_1_out0, decoder_1_out1, decoder_1_out2, decoder_1_out3, decoder_1_out4, decoder_1_out5,
       decoder_1_out6, decoder_1_out7;

  Decoder #(.select(3)) decoder_1 (
    .out0(decoder_1_out0), .out1(decoder_1_out1), .out2(decoder_1_out2), .out3(decoder_1_out3),
    .out4(decoder_1_out4), .out5(decoder_1_out5), .out6(decoder_1_out6), .out7(decoder_1_out7), .sel(SC));  // open: en
  and and_1 (Load, ~R, decoder_1_out1);  // AND_Gate
endmodule

// Tiiming decoder
module Timing_decoder (
  input  Counter_Input,
  output out_2,
  output out_3,
  output out_4,
  output out_5,
  output out_6,
  output out_7,
  output out_8,
  output out_9
);

  wire button_1_out, clock_1_out;
  wire [2:0] counter_1_q;

  Clock clock_1 (.out(clock_1_out));
  Counter #(.width(3), .max('h7)) counter_1 (
    .load(Counter_Input), .Q(counter_1_q), .clk(clock_1_out), .clr(button_1_out));  // open: D, count, carry
  Button button_1 (.out(button_1_out));
  Decoder #(.select(3)) decoder_1 (
    .out0(out_2), .out1(out_3), .out2(out_4), .out3(out_5), .out4(out_6), .out5(out_7), .out6(out_8),
    .out7(out_9), .sel(counter_1_q));  // open: en
endmodule

// BUS Control
module Bus_Control (
  input  [19:0] IR,
  input  R,
  input  [2:0] SC,
  output [2:0] out_4
);

  wire and_1_out, and_2_out, and_3_out, and_4_out, and_5_out, and_6_out, and_7_out, and_8_out, and_9_out,
       and_10_out, and_11_out, and_12_out, and_13_out, and_14_out, and_15_out, and_17_out, and_18_out,
       and_19_out, and_20_out, and_21_out, decoder_1_out0, decoder_1_out1, decoder_1_out2, decoder_1_out3,
       decoder_1_out4, decoder_1_out5, decoder_1_out6, decoder_1_out7, decoder_2_out0, decoder_2_out1,
       decoder_2_out2, decoder_2_out3, decoder_2_out4, decoder_2_out5, decoder_2_out6, decoder_2_out7,
       decoder_2_out8, decoder_2_out9, decoder_2_out10, decoder_2_out11, decoder_2_out12, decoder_2_out13,
       decoder_2_out14, decoder_2_out15, or_1_out, or_2_out, or_3_out, or_4_out, or_5_out, or_6_out, p;

  Decoder #(.select(3)) decoder_1 (
    .out0(decoder_1_out0), .out1(decoder_1_out1), .out2(decoder_1_out2), .out3(decoder_1_out3),
    .out4(decoder_1_out4), .out5(decoder_1_out5), .out6(decoder_1_out6), .out7(decoder_1_out7), .sel(SC));  // open: en
  Decoder #(.select(4)) decoder_2 (
    .out0(decoder_2_out0), .out1(decoder_2_out1), .out2(decoder_2_out2), .out3(decoder_2_out3),
    .out4(decoder_2_out4), .out5(decoder_2_out5), .out6(decoder_2_out6), .out7(decoder_2_out7),
    .out8(decoder_2_out8), .out9(decoder_2_out9), .out10(decoder_2_out10), .out11(decoder_2_out11),
    .out12(decoder_2_out12), .out13(decoder_2_out13), .out14(decoder_2_out14), .out15(decoder_2_out15),
    .sel(IR[17:14]));  // open: en
  and and_1 (and_1_out, decoder_2_out6, decoder_1_out5);
  and and_2 (and_2_out, decoder_2_out7, decoder_1_out6);
  and and_3 (and_3_out, R, decoder_1_out0);
  and and_4 (and_4_out, R, decoder_1_out1);
  and and_5 (and_5_out, decoder_2_out7, decoder_1_out5);
  and and_6 (and_6_out, decoder_2_out4, decoder_1_out5);
  and and_7 (and_7_out, decoder_2_out8, decoder_1_out6);
  and and_8 (and_8_out, decoder_2_out9, decoder_1_out6);
  and and_9 (and_9_out, decoder_2_out5, decoder_1_out5);
  and and_10 (and_10_out, decoder_2_out9, decoder_1_out5);
  and and_11 (and_11_out, IR[12], p);
  and and_12 (and_12_out, ~R, decoder_1_out2);  // AND_Gate
  and and_13 (and_13_out, R, decoder_1_out2);
  and and_14 (and_14_out, decoder_2_out9, decoder_1_out6);
  and and_15 (and_15_out, ~R, decoder_1_out1);  // AND_Gate
  and and_16 (p, decoder_1_out3, IR[19], IR[18], decoder_2_out15);
  and and_17 (and_17_out, ~decoder_2_out0, ~decoder_2_out15, decoder_1_out3, IR[19], ~IR[18]);  // AND_Gate
  and and_18 (and_18_out, ~decoder_2_out0, ~decoder_2_out15, decoder_1_out3, ~IR[19], ~IR[18]);  // AND_Gate
  and and_19 (and_19_out, ~decoder_2_out0, ~decoder_2_out15, decoder_1_out3, ~IR[19], IR[18]);  // AND_Gate
  and and_20 (and_20_out, ~decoder_2_out0, ~decoder_2_out15, decoder_1_out4, ~IR[19], IR[18]);  // AND_Gate
  or or_1 (or_1_out, and_6_out, and_7_out, and_8_out);
  or or_2 (or_2_out, and_9_out, and_10_out, and_11_out);
  or or_3 (or_3_out, and_13_out, and_14_out);
  or or_4 (or_4_out, and_17_out, and_1_out, and_2_out);
  or or_5 (or_5_out, and_3_out, and_4_out, and_5_out);
  and and_21 (and_21_out, ~or_4_out, ~or_5_out, ~or_1_out, ~or_2_out, ~and_12_out, ~or_3_out, ~or_6_out);  // AND_Gate
  or or_6 (or_6_out, and_15_out, and_18_out, and_19_out, and_20_out);
  Priority_Encoder priority_encoder_1 (
    .in0(and_21_out), .in1(or_4_out), .in2(or_5_out), .in3(or_1_out), .in4(or_2_out), .in5(and_12_out),
    .in6(or_3_out), .in7(or_6_out), .out(out_4));  // open: en_in, gs, en_out
endmodule

module Final (
  input  [19:0] IR,
  input  R,
  input  Counter_Input,
  output [19:0] out_4,
  output [2:0] out_5
);

  wire ac_control_1_clear, ac_control_1_increment, ac_control_1_load, ar_control_1_clear,
       ar_control_1_increment, ar_control_1_load, button_1_out, clock_1_out, dr_control_1_increment,
       dr_control_1_load, ir_control_1_load, memory_control_1_read, memory_control_1_write,
       pc_control_1_clear, pc_control_1_increment, pc_control_1_load, tr_control_1_load;
  wire [2:0] counter_1_q;
  wire [19:0] ac_1_output, ar_1_out, dr_1_out_5, ir_1_out_4, memory_1_output, pc_1_out, tr_1_output;

  Clock clock_1 (.out(clock_1_out));
  Counter #(.width(3), .max('h7)) counter_1 (
    .load(Counter_Input), .Q(counter_1_q), .clk(clock_1_out), .clr(button_1_out));  // open: D, count, carry
  Button button_1 (.out(button_1_out));
  Memory_Control memory_control_1 (
    .R(R), .IR(ir_1_out_4), .Write(memory_control_1_write), .SC(counter_1_q), .Read(memory_control_1_read));
  Memory memory_1 (
    .AR(ar_1_out), .Output(memory_1_output), .CBS_Mockup(out_4), .Read(memory_control_1_read),
    .Clock(clock_1_out), .Write(memory_control_1_write));
  AR_control ar_control_1 (
    .Load(ar_control_1_load), .Clear(ar_control_1_clear), .Increment(ar_control_1_increment), .R(R),
    .IR(ir_1_out_4), .SC(counter_1_q));
  PC_control pc_control_1 (
    .IR(ir_1_out_4), .Load(pc_control_1_load), .Increment(pc_control_1_increment),
    .Clear(pc_control_1_clear), .SC(counter_1_q), .R(R), .AC(ac_1_output), .DR(dr_1_out_5));  // open: FGI, FGO, E
  DR_control dr_control_1 (
    .IR(dr_1_out_5), .SC(counter_1_q), .Load(dr_control_1_load), .Increment(dr_control_1_increment));
  DR dr_1 (
    .in_4(clock_1_out), .out_5(dr_1_out_5), .CBS_Mockup(out_4), .Incr(dr_control_1_load),
    .Load(dr_control_1_increment));
  AC_control ac_control_1 (
    .Clear(ac_control_1_clear), .Increment(ac_control_1_increment), .SC(counter_1_q), .IR(ir_1_out_4),
    .Load(ac_control_1_load));
  AC ac_1 (
    .in_5(clock_1_out), .Output(ac_1_output), .Incr(ac_control_1_increment), .Load(ac_control_1_load),
    .Clear(ac_control_1_clear));  // open: ALU
  IR_control ir_control_1 (.R(R), .Load(ir_control_1_load), .SC(counter_1_q));
  IR ir_1 (.Load(ir_control_1_load), .in_3(clock_1_out), .out_4(ir_1_out_4), .CBS_Mockup(IR));
  TR_control tr_control_1 (.SC(counter_1_q), .R(R), .IR(ir_1_out_4), .Load(tr_control_1_load));
  TR tr_1 (.Load(tr_control_1_load), .in_3(clock_1_out), .Output(tr_1_output), .CBS(out_4));
  AR ar_1 (
    .OUT(ar_1_out), .Load(ar_control_1_load), .Clear(ar_control_1_clear), .INcrement(ar_control_1_increment),
    .Clk(clock_1_out), .Common_Bus(out_4));
  PC pc_1 (
    .in_5(clock_1_out), .Common_Bus(out_4), .OUT(pc_1_out), .in_2(pc_control_1_clear),
    .in_3(pc_control_1_load), .in_4(pc_control_1_increment));
  Bus_Control bus_control_1 (.SC(counter_1_q), .IR(IR), .R(R), .out_4(out_5));
  Multiplexer #(.select(3), .width(20), .enable("false")) multiplexer_1 (
    .in0({20{1'b0}}), .in1(ar_1_out), .in2(pc_1_out), .in3(dr_1_out_5), .in4(ac_1_output), .in5(ir_1_out_4),
    .in6(tr_1_output), .in7(memory_1_output), .out(out_4), .sel(out_5));
  Hex_Digit_Display hex_digit_display_1 (.value(out_4[15:12]));  // open: dp
  Hex_Digit_Display hex_digit_display_2 (.value(out_4[19:16]));  // open: dp
  Hex_Digit_Display hex_digit_display_3 (.value(memory_1_output[19:16]));  // open: dp
  Hex_Digit_Display hex_digit_display_4 (.value(ar_1_out[19:16]));  // open: dp
  Hex_Digit_Display hex_digit_display_5 (.value(pc_1_out[19:16]));  // open: dp
  Hex_Digit_Display hex_digit_display_6 (.value(dr_1_out_5[19:16]));  // open: dp
  Hex_Digit_Display hex_digit_display_7 (.value(ac_1_output[19:16]));  // open: dp
  Hex_Digit_Display hex_digit_display_8 (.value(ir_1_out_4[19:16]));  // open: dp
  Hex_Digit_Display hex_digit_display_9 (.value(tr_1_output[19:16]));  // open: dp
  Hex_Digit_Display hex_digit_display_10 (.value(out_4[11:8]));  // open: dp
  Hex_Digit_Display hex_digit_display_11 (.value(memory_1_output[11:8]));  // open: dp
  Hex_Digit_Display hex_digit_display_12 (.value(memory_1_output[15:12]));  // open: dp
  Hex_Digit_Display hex_digit_display_13 (.value(ar_1_out[11:8]));  // open: dp
  Hex_Digit_Display hex_digit_display_14 (.value(ar_1_out[15:12]));  // open: dp
  Hex_Digit_Display hex_digit_display_15 (.value(pc_1_out[11:8]));  // open: dp
  Hex_Digit_Display hex_digit_display_16 (.value(pc_1_out[15:12]));  // open: dp
  Hex_Digit_Display hex_digit_display_17 (.value(dr_1_out_5[11:8]));  // open: dp
  Hex_Digit_Display hex_digit_display_18 (.value(dr_1_out_5[15:12]));  // open: dp
  Hex_Digit_Display hex_digit_display_19 (.value(ac_1_output[15:12]));  // open: dp
  Hex_Digit_Display hex_digit_display_20 (.value(ac_1_output[11:8]));  // open: dp
  Hex_Digit_Display hex_digit_display_21 (.value(ir_1_out_4[11:8]));  // open: dp
  Hex_Digit_Display hex_digit_display_22 (.value(ir_1_out_4[15:12]));  // open: dp
  Hex_Digit_Display hex_digit_display_23 (.value(tr_1_output[15:12]));  // open: dp
  Hex_Digit_Display hex_digit_display_24 (.value(out_4[7:4]));  // open: dp
  Hex_Digit_Display hex_digit_display_25 (.value(out_4[3:0]));  // open: dp
  Hex_Digit_Display hex_digit_display_26 (.value(memory_1_output[7:4]));  // open: dp
  Hex_Digit_Display hex_digit_display_27 (.value(memory_1_output[3:0]));  // open: dp
  Hex_Digit_Display hex_digit_display_28 (.value(ar_1_out[7:4]));  // open: dp
  Hex_Digit_Display hex_digit_display_29 (.value(ar_1_out[3:0]));  // open: dp
  Hex_Digit_Display hex_digit_display_30 (.value(pc_1_out[7:4]));  // open: dp
  Hex_Digit_Display hex_digit_display_31 (.value(dr_1_out_5[7:4]));  // open: dp
  Hex_Digit_Display hex_digit_display_32 (.value(ac_1_output[7:4]));  // open: dp
  Hex_Digit_Display hex_digit_display_33 (.value(ir_1_out_4[7:4]));  // open: dp
  Hex_Digit_Display hex_digit_display_34 (.value(tr_1_output[7:4]));  // open: dp
  Hex_Digit_Display hex_digit_display_35 (.value(tr_1_output[11:8]));  // open: dp
  Hex_Digit_Display hex_digit_display_36 (.value(pc_1_out[3:0]));  // open: dp
  Hex_Digit_Display hex_digit_display_37 (.value(dr_1_out_5[3:0]));  // open: dp
  Hex_Digit_Display hex_digit_display_38 (.value(ac_1_output[3:0]));  // open: dp
  Hex_Digit_Display hex_digit_display_39 (.value(ir_1_out_4[3:0]));  // open: dp
  Hex_Digit_Display hex_digit_display_40 (.value(tr_1_output[3:0]));  // open: dp

  // Notes on the sheet:
  //   Flip flop haru add garna baki xa+etc
  //   Common Bus
endmodule

module Memory (
  input  [19:0] AR,
  input  [19:0] CBS_Mockup,
  input  Write,
  input  Clock,
  input  Read,
  output [19:0] Output
);

  RAM #(.addrWidth(14), .dataWidth(20), .bus("separate")) ram_1 (
    .addr(AR[13:0]), .din(CBS_Mockup), .data(Output), .str(Write), .clk(Clock), .ld(Read));  // open: sel, clr
endmodule

module Memory_Control (
  input  [19:0] IR,
  input  R,
  input  [2:0] SC,
  output Write,
  output Read
);

  wire and_1_out, and_2_out, and_3_out, and_4_out, and_5_out, and_6_out, and_7_out, and_8_out,
       decoder_1_out0, decoder_1_out1, decoder_1_out2, decoder_1_out3, decoder_1_out4, decoder_1_out5,
       decoder_1_out6, decoder_1_out7, decoder_2_out0, decoder_2_out1, decoder_2_out2, decoder_2_out3,
       decoder_2_out4, decoder_2_out5, decoder_2_out6, decoder_2_out7, decoder_2_out8, decoder_2_out9,
       decoder_2_out10, decoder_2_out11, decoder_2_out12, decoder_2_out13, decoder_2_out14, decoder_2_out15;

  Decoder #(.select(3), .enable("false")) decoder_1 (
    .out0(decoder_1_out0), .out1(decoder_1_out1), .out2(decoder_1_out2), .out3(decoder_1_out3),
    .out4(decoder_1_out4), .out5(decoder_1_out5), .out6(decoder_1_out6), .out7(decoder_1_out7), .sel(SC));
  Decoder #(.select(4), .enable("false")) decoder_2 (
    .out0(decoder_2_out0), .out1(decoder_2_out1), .out2(decoder_2_out2), .out3(decoder_2_out3),
    .out4(decoder_2_out4), .out5(decoder_2_out5), .out6(decoder_2_out6), .out7(decoder_2_out7),
    .out8(decoder_2_out8), .out9(decoder_2_out9), .out10(decoder_2_out10), .out11(decoder_2_out11),
    .out12(decoder_2_out12), .out13(decoder_2_out13), .out14(decoder_2_out14), .out15(decoder_2_out15),
    .sel(IR[17:14]));
  and and_1 (and_1_out, ~R, decoder_1_out1);  // AND_Gate
  and and_2 (and_2_out, R, decoder_1_out2);
  and and_3 (and_3_out, decoder_1_out5, decoder_2_out5);
  and and_4 (and_4_out, decoder_1_out5, decoder_2_out7);
  and and_5 (and_5_out, decoder_2_out8, decoder_1_out6);
  and and_6 (and_6_out, ~decoder_2_out0, ~decoder_2_out15, decoder_1_out3, ~IR[19], ~IR[18]);  // AND_Gate
  and and_7 (and_7_out, ~decoder_2_out0, ~decoder_2_out15, decoder_1_out4, ~IR[18], IR[18]);  // AND_Gate
  and and_8 (and_8_out, ~decoder_2_out0, ~decoder_2_out15, decoder_1_out3, ~IR[19], IR[18]);  // AND_Gate
  or or_1 (Write, and_2_out, and_3_out, and_4_out, and_5_out);
  or or_2 (Read, and_1_out, and_6_out, and_7_out, and_8_out);
endmodule

module pc_KO_LAGI (
  input  [19:0] AC,
  input  [19:0] DR,
  input  FGO,
  input  FGI,
  input  R,
  input  E,
  input  [2:0] in_7
);

  wire pc_control_1_p8;

  // PC_control pc_control_1: pin names not known; wires that end beside it: in_7, R, FGI, FGO, E, AC, DR, pc_control_1_p8
endmodule

module shift (
  input  [19:0] in_1,
  input  [4:0] in_2,
  output [19:0] out_3
);

  Shifter #(.width(20)) shifter_1 (.in(in_1), .\dist (in_2), .out(out_3));
endmodule

module TR (
  input  [19:0] CBS,
  input  Load,
  input  in_3,
  output [19:0] Output
);

  wire button_1_out;

  Button button_1 (.out(button_1_out));
  Register #(.width(20)) TR (.D(CBS), .en(Load), .Q(Output), .clk(in_3), .clr(button_1_out));
endmodule

module TR_control (
  input  [2:0] SC,
  input  [19:0] IR,
  input  R,
  output Load
);

  wire and_1_out, and_2_out, decoder_1_out1, decoder_1_out5, decoder_2_out9;

  Decoder #(.select(3), .enable("false")) decoder_1 (
    .out1(decoder_1_out1), .out5(decoder_1_out5), .sel(SC));  // open: out0, out2, out3, out4, out6, out7
  Decoder #(.select(4), .enable("false")) decoder_2 (
    .out9(decoder_2_out9), .sel(IR[17:14]));  // open: out0, out1, out2, out3, out4, out5, out6, out7, out8, out10, out11, out12, out13, out14, out15
  and and_1 (and_1_out, decoder_1_out1, R);
  and and_2 (and_2_out, decoder_1_out5, decoder_2_out9);
  or or_1 (Load, and_1_out, and_2_out);

  // Notes on the sheet:
  //   3x8 decoder
  //   4x16 decoder
endmodule

module I0_flip_flop (
  input  R,
  input  [19:0] IR,
  input  [2:0] SC,
  input  clk,
  output I0_Value
);

  wire i0_flip_flop_control_1_j, i0_flip_flop_control_1_k;

  I0_Flip_flop_control i0_flip_flop_control_1 (
    .SC(SC), .J(i0_flip_flop_control_1_j), .K(i0_flip_flop_control_1_k), .IR(IR), .R(R));
  J_K_Flip_Flop I0 (
    .J(i0_flip_flop_control_1_j), .clk(clk), .K(i0_flip_flop_control_1_k), .Q(I0_Value));  // open: Qn, preset, en, reset
endmodule

// I0 Flip-flop Control
module I0_Flip_flop_control (
  input  [2:0] SC,
  input  R,
  input  [19:0] IR,
  output J,
  output K
);

  wire and_1_out, decoder_1_out2, not_1_out, not_2_out;

  Decoder #(.select(3), .enable("false")) decoder_1 (
    .out2(decoder_1_out2), .sel(SC));  // open: out0, out1, out3, out4, out5, out6, out7
  not not_1 (not_1_out, R);
  and and_1 (and_1_out, decoder_1_out2, not_1_out);
  not not_2 (not_2_out, IR[18]);
  and and_2 (J, and_1_out, IR[18]);
  and and_3 (K, and_1_out, not_2_out);

  // Notes on the sheet:
  //   3x8 decoder
endmodule

module I1_Flip_flop (
  input  R,
  input  [19:0] IR,
  input  [2:0] SC,
  input  clk,
  output I1_value
);

  wire i1_flip_flop_control_1_j, i1_flip_flop_control_1_k;

  I1_Flip_flop_control i1_flip_flop_control_1 (
    .SC(SC), .R(R), .J(i1_flip_flop_control_1_j), .K(i1_flip_flop_control_1_k), .IR(IR));
  J_K_Flip_Flop I1 (
    .J(i1_flip_flop_control_1_j), .clk(clk), .K(i1_flip_flop_control_1_k), .Q(I1_value));  // open: Qn, preset, en, reset
endmodule

module I1_Flip_flop_control (
  input  [2:0] SC,
  input  R,
  input  [19:0] IR,
  output J,
  output K
);

  wire and_1_out, decoder_1_out2, not_1_out, not_2_out;

  Decoder #(.select(3), .enable("false")) decoder_1 (
    .out2(decoder_1_out2), .sel(SC));  // open: out0, out1, out3, out4, out5, out6, out7
  not not_1 (not_1_out, R);
  and and_1 (and_1_out, decoder_1_out2, not_1_out);
  not not_2 (not_2_out, IR[19]);
  and and_2 (J, and_1_out, IR[19]);
  and and_3 (K, and_1_out, not_2_out);

  // Notes on the sheet:
  //   3x8 decoder
endmodule

module R_Flip_flop_control (
  input  [2:0] SC,
  input  R,
  input  IEN,
  input  FGI,
  input  FGO,
  output K,
  output J
);

  wire decoder_1_out0, decoder_1_out1, decoder_1_out2, decoder_1_out3, not_1_out, not_2_out, not_3_out,
       or_1_out;

  Decoder #(.select(3), .enable("false")) decoder_1 (
    .out0(decoder_1_out0), .out1(decoder_1_out1), .out2(decoder_1_out2), .out3(decoder_1_out3), .sel(SC));  // open: out4, out5, out6, out7
  not not_1 (not_1_out, decoder_1_out2);
  not not_2 (not_2_out, decoder_1_out1);
  not not_3 (not_3_out, decoder_1_out0);
  or or_1 (or_1_out, FGI, FGO);
  and and_1 (K, R, decoder_1_out3);
  and and_2 (J, not_1_out, not_2_out, not_3_out, IEN, or_1_out);

  // Notes on the sheet:
  //   3x8 decoder
endmodule

module R_Flip_flop (
  input  FGO,
  input  FGI,
  input  IEN,
  input  [2:0] SC,
  input  in_5,
  output R_value
);

  wire r_flip_flop_control_1_j, r_flip_flop_control_1_k;

  R_Flip_flop_control r_flip_flop_control_1 (
    .SC(SC), .R(R_value), .IEN(IEN), .FGI(FGI), .FGO(FGO), .K(r_flip_flop_control_1_k),
    .J(r_flip_flop_control_1_j));
  J_K_Flip_Flop R (
    .J(r_flip_flop_control_1_j), .clk(in_5), .K(r_flip_flop_control_1_k), .Q(R_value));  // open: Qn, preset, en, reset
endmodule

module IEN_Flip_flop (
  input  [19:0] IR,
  input  R,
  input  I1,
  input  [2:0] SC,
  input  I0,
  input  clk,
  output IEN_value
);

  wire ien_flip_flop_control_1_j, ien_flip_flop_control_1_k;

  IEN_Flip_flop_control ien_flip_flop_control_1 (
    .SC(SC), .R(R), .IR(IR), .J(ien_flip_flop_control_1_j), .K(ien_flip_flop_control_1_k), .I0(I0), .I1(I1));
  J_K_Flip_Flop IEN (
    .J(ien_flip_flop_control_1_j), .clk(clk), .K(ien_flip_flop_control_1_k), .Q(IEN_value));  // open: Qn, preset, en, reset
endmodule

module IEN_Flip_flop_control (
  input  [2:0] SC,
  input  [19:0] IR,
  input  I0,
  input  I1,
  input  R,
  output J,
  output K
);

  wire and_3_out, and_4_out, decoder_1_out3, decoder_2_out15, p;

  Decoder #(.select(3), .enable("false")) decoder_1 (
    .out3(decoder_1_out3), .sel(SC));  // open: out0, out1, out2, out4, out5, out6, out7
  Decoder #(.select(4), .enable("false")) decoder_2 (
    .out15(decoder_2_out15), .sel(IR[17:14]));  // open: out0, out1, out2, out3, out4, out5, out6, out7, out8, out9, out10, out11, out12, out13, out14
  and and_1 (p, decoder_2_out15, decoder_1_out3, I0, I1);
  and and_2 (J, IR[9], p);
  and and_3 (and_3_out, p, IR[8]);
  and and_4 (and_4_out, R, decoder_1_out3);
  or or_1 (K, and_3_out, and_4_out);

  // Notes on the sheet:
  //   3x8 decoder
  //   4x16 decoder
endmodule
